# Fritzing sketch v3 (saved by Fritzing 0.9.3b)
circuit board: 4.82cm x 4.32cm
breadboards: 1

parts:
  BMP+MPU = male pin header, 4 pins [form="♂ (male)"]
  GPS = female pin header, 4 pins [form="♀ (female)"]
  R1 = Resistor [tolerance=±5% resistance=4.7 package=THT]
  Teensy_3_1 = Teensy 3.1
  DS1 = DS18B20 1-Wire Temperature Sensor [part_number=DS18B20]
  Part1 = NRF24L01+ Breakout Board
  J1 = female pin header, 3 pins [form="♀ (female)"]
  J2 = female pin header, 3 pins [form="♀ (female)"]
  R3 = Resistor [tolerance=±5% resistance=220 package=THT]
  R2 = Resistor [tolerance=±5% resistance=10k package=THT]
  J3 = female pin header, 7 pins [form="♀ (female)"]
  Battery = female pin header, 2 pins [form="♀ (female)"]
  J12 = female pin header, 3 pins [form="♀ (female)"]  # not connected
  R5 = Resistor [tolerance=±5% resistance=220 package=THT]
  R6 = Resistor [tolerance=±5% resistance=220 package=THT]
  Part2 = OpenLog
  LED1 = LED - 3mm [color="Red (633nm)" package="3 mm [THT]"]
  J13 = female pin header, 2 pins [form="♀ (female)"]
  R7 = Photocell (LDR) [package=THT]
  R9 = PHOTOCELL [package=photocell-kit]
  J14 = female pin header, 2 pins [form="♀ (female)"]
  J8 = female pin header, 3 pins [form="♀ (female)"]
  J4 = female pin header, 3 pins [form="♀ (female)"]

nets:
  SDA: BMP+MPU.pin1, Teensy_3_1.A4/D18
  SCL: BMP+MPU.pin2, Teensy_3_1.A5/D19
  GND: BMP+MPU.pin3, GPS.pin2, R1.Pin_0, Teensy_3_1.GND, DS1.GND, Part1.GND, J1.pin3, J2.pin3, R3.Pin_0, J3.pin2, J3.pin3, Battery.pin2, R6.Pin_0, Part2.GND, LED1.cathode, R7.pin_1, J8.pin2, J4.pin2
  3.3V: BMP+MPU.pin4, GPS.pin1, Teensy_3_1.3V3#30, R9.P$2, J4.pin1
  RX1: GPS.pin3, Teensy_3_1.D0
  TX1: GPS.pin4, Teensy_3_1.D1
  VCC: R1.Pin_1, Teensy_3_1.3V3#15, DS1.VDD, Part1.VCC, Part2.VCC
  N1: Teensy_3_1.D2, DS1.DQ
  N2: Teensy_3_1.D3, J1.pin1, J2.pin1
  N3: Teensy_3_1.D4, LED1.anode
  N4: Teensy_3_1.D5, Part1.CE
  N5: Teensy_3_1.D6, Part1.CS
  RX3: Teensy_3_1.D7, J13.pin2
  TX3: Teensy_3_1.D8, J13.pin1
  N6: Teensy_3_1.D9, Part2.TXO
  N7: Teensy_3_1.D10, Part2.RXI
  N8: Teensy_3_1.D11, Part1.MOSI
  N9: Teensy_3_1.D12, Part1.MISO
  N10: Teensy_3_1.D13, Part1.SCK
  N11: Teensy_3_1.A0/D14, R2.Pin_0, Battery.pin1, J8.pin3, J4.pin3
  N12: Teensy_3_1.A1/D15, J3.pin1, R5.Pin_0
  N13: Teensy_3_1.A2/D16, R3.Pin_1, R2.Pin_1
  N14: Teensy_3_1.A3/D17, R5.Pin_1, R6.Pin_1
  N15: Teensy_3_1.A6/D20, J14.pin1
  N16: Teensy_3_1.A7/D21, J14.pin2
  N17: Teensy_3_1.A8/D22, R7.pin_0, R9.P$1
  N18: J1.pin2, J2.pin2, J8.pin1

notes:
  ITURRAMASAT
  TOP
  BTN
  v3
